# Fritzing sketch CV_schematic (saved by Fritzing 0.9.9b)
breadboards: 1

parts:
  U1 = MCP4725 [package=SOT23-6]
  U2 = LF412 [package=dip08]
  Part2 = Adafruit ADS1015 12Bit I2C ADC [part_number="Adafruit #1083"]
  JP3 = Header 3 [package=molex-1x3_lock]
  U3 = LF412 [package=dip08]
  R5 = Resistor [tolerance=±5% power=0.25 resistance=40k package=THT]
  R6 = Resistor [tolerance=±5% power=0.25 resistance=10k package=THT]
  R7 = Resistor [tolerance=±5% power=0.25 resistance=10k package=THT]
  R8 = Resistor [tolerance=±5% power=0.25 resistance=10k package=THT]
  R9 = Resistor [tolerance=±5% power=0.25 resistance=10k package=THT]
  R10 = Resistor [tolerance=±5% power=0.25 resistance=10k package=THT]
  U4 = LF412 [package=dip08]
  R11 = Resistor [tolerance=±5% power=0.25 resistance=10k package=THT]
  R12 = Resistor [tolerance=±5% power=0.25 resistance=10k package=THT]
  R15 = Resistor [tolerance=±5% power=0.25 resistance=10k package=THT]
  R16 = Resistor [tolerance=±5% power=0.25 resistance=10k package=THT]
  R17 = Resistor [tolerance=±5% power=0.25 resistance=10k package=THT]
  Part1 = Arduino Uno (Rev3)
  R18 = Resistor [tolerance=±5% power=0.25 resistance=10k package=THT]

nets (from the breadboard view):
  VDD: U1.VDD, U2.G$1_V+, Part2.VDD, U3.G$1_V+, R5.Pin_1, U4.G$1_V+, Part1.5V
  GND: U1.VSS, U2.G$1_+IN, Part2.GND, R8.Pin_0, R10.Pin_0, R17.Pin_1, Part1.GND
  N1: U1.VOUT, Part2.AIN0, R8.Pin_1, R9.Pin_1
  N2: U1.SCL, Part1.A5/SCL
  N3: U1.SDA, Part1.A4/SDA
  N4: U2.G$1_OUT, R11.Pin_0, R16.Pin_1, R17.Pin_0
  N5: U2.G$1_-IN, JP3.WE, R11.Pin_1
  N6: U2.G$1_V-, U3.G$1_V-, U4.G$1_V-, R18.Pin_1
  N7: U2.G$2_+IN, U3.G$2_OUT, R6.Pin_0
  N8: U2.G$2_-IN, JP3.RE
  N9: U2.G$2_OUT, JP3.CE
  N10: Part2.AIN1, U3.G$1_OUT
  N11: U3.G$1_-IN, R15.Pin_0
  N12: U3.G$1_+IN, R16.Pin_0
  N13: U3.G$2_+IN, R9.Pin_0
  N14: U3.G$2_-IN, R6.Pin_1, R7.Pin_0
  N15: R5.Pin_0, R10.Pin_1, U4.G$2_+IN
  N16: R7.Pin_1, U4.G$2_-IN, U4.G$2_OUT
  N17: U4.G$1_OUT, U4.G$1_-IN, R15.Pin_1
  N18: U4.G$1_+IN, R12.Pin_0

custom parts:
  LF412: Jellybean op-amp
  Adafruit ADS1015 12Bit I2C ADC: For microcontrollers without an analog-to-digital converter or when you want a higher-precision ADC, the ADS1015 provides 12-bit precision at 3300 samples/second over I2C. The chip can be configured as 4 single-ended input channels, or two differential channels. As a nice bonus, it even includes a programmable gain amplifier, up to x16, to help boost up smaller single/differential signals to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
  Header 3: Header 3 Standard 3-pin 0.1 header. Use with straight break away headers (SKU : PRT-00116), right angle break away headers (PRT-00553), swiss pins (PRT-00743), machine pins (PRT-00117), and female headers (PRT-00115). Molex polarized connector foot print use with SKU : PRT-08232 with associated crimp pins and housings.
